# Fritzing sketch ultrasono bt-control bot (saved by Fritzing 0.9.2b)
breadboards: 1

parts:
  Part1 = Bluetooth HC-05 Macho  # not connected
  IC1 = L293D [package=THT]
  Part2 = Arduino Uno (Rev3)
  M1 = DC Motor
  M2 = DC Motor
  U3 = HC-SR04 [chip_label=IC package="SIP (Single Inline) [THT]"]
  Battery1 = Battery block 9V

nets:
  N1: IC1.Enable_1, IC1.Enable_2, IC1.+V, U3.Vcc
  N2: IC1.In_1, Part2.D3_PWM
  N3: IC1.Out_1_(_Controlled_by_Enable_1_), M2.pin_2
  GND: IC1.0V, IC1.+Vmotor, Part2.GND, U3.GND, Battery1.-
  N4: IC1.Out_2_(_Controlled_by_Enable_1_), M2.pin_1
  N5: IC1.In_2, Part2.D4
  N6: IC1.In_3, Part2.D8
  N7: IC1.Out_3_(_Controlled_by_Enable_2_), M1.pin_2
  N8: IC1.Out_4_(_Controlled_by_Enable_2_), M1.pin_1
  N9: IC1.In_4, Part2.D9_PWM
  N10: Part2.D11_PWM/MOSI, U3.Trig
  N11: Part2.D12/MISO, U3.Echo
  N12: Part2.VIN, Battery1.+

custom parts:
  HC-SR04: HC-SR04 ultrasound distance sensor
